# Fritzing sketch ultrasonic (saved by Fritzing 1.0.0d)

parts:
  Деталь1 = Arduino Mega Sensor Shield v2.0
  HC-SR04_Sensor_1 = HC-SR04 Ultrasonic Distance Sensor
  S1 = 0.91 inch OLED I2C Display 128 x 32 Pixels

nets:
  N1: Деталь1.pin_26, Деталь1.pin_165, HC-SR04_Sensor_1.TRIG
  N2: Деталь1.pin_27, Деталь1.pin_162, HC-SR04_Sensor_1.ECHO
  N3: Деталь1.pin_38, Деталь1.pin_273, S1.SCL
  N4: Деталь1.pin_39, Деталь1.pin_270, S1.SDA
  GND: Деталь1.pin_82, Деталь1.pin_160, Деталь1.pin_271, HC-SR04_Sensor_1.GND, S1.GND
  VCC: Деталь1.pin_83, Деталь1.pin_161, Деталь1.pin_272, HC-SR04_Sensor_1.VCC, S1.VCC
